// Logisim project Design Simulation.circ as structural Verilog: 2 circuits, main circuit main
module main (
  input  Reset,
  input  SFD,
  input  SRD,
  input  SFA,
  input  SW,
  input  STG,
  input  STL,
  output out_8,
  output out_9,
  output out_10
);

  wire clock_1_out, priority_encoder_1_a0, priority_encoder_1_a1, priority_encoder_1_a2;

  priority_encoder priority_encoder_1 (
    .Reset(Reset), .SFD(SFD), .SRD(SRD), .SFA(SFA), .SW(SW), .STG(STG), .STL(STL),
    .A2(priority_encoder_1_a2), .A1(priority_encoder_1_a1), .A0(priority_encoder_1_a0));
  Clock clock_1 (.out(clock_1_out));
  D_Flip_Flop d_ff_1 (.clk(clock_1_out), .D(priority_encoder_1_a2), .Q(out_8), .en(1'b1));  // open: Qn, preset, reset
  D_Flip_Flop d_ff_2 (.clk(clock_1_out), .D(priority_encoder_1_a1), .Q(out_9), .en(1'b1));  // open: Qn, preset, reset
  D_Flip_Flop d_ff_3 (.clk(clock_1_out), .D(priority_encoder_1_a0), .Q(out_10), .en(1'b1));  // open: Qn, preset, reset
endmodule

module priority_encoder (
  input  Reset,
  input  SFD,
  input  SRD,
  input  SFA,
  input  SW,
  input  STG,
  input  STL,
  output A2,
  output A1,
  output A0
);

  wire nand_1_out, nand_2_out, nand_3_out, nand_4_out, nand_5_out, nand_6_out, nand_7_out, nand_8_out,
       nand_9_out, nand_10_out, nand_11_out, nand_12_out, nand_13_out, nand_14_out, nand_15_out, nand_16_out,
       nand_17_out, nand_18_out, nand_19_out, nand_20_out, nand_21_out, nand_22_out, nand_23_out,
       nand_24_out, nand_25_out, nand_26_out, nand_27_out, nand_28_out, nand_29_out, nand_30_out,
       nand_31_out, nand_32_out, nand_33_out, nand_34_out;

  nand nand_1 (nand_1_out, Reset, Reset);
  nand nand_2 (nand_2_out, SFD, SFD);
  nand nand_3 (nand_3_out, SRD, SRD);
  nand nand_4 (nand_4_out, SFA, SFA);
  nand nand_5 (nand_5_out, Reset, Reset);
  nand nand_6 (nand_6_out, SFD, SFD);
  nand nand_7 (nand_7_out, SRD, SRD);
  nand nand_8 (nand_8_out, SFA, SFA);
  nand nand_9 (nand_9_out, Reset, Reset);
  nand nand_10 (nand_10_out, SFD, SFD);
  nand nand_11 (nand_11_out, SRD, SRD);
  nand nand_12 (nand_12_out, SFA, SFA);
  nand nand_13 (nand_13_out, Reset, Reset);
  nand nand_14 (nand_14_out, SFD, SFD);
  nand nand_15 (nand_15_out, SW, SW);
  nand nand_16 (nand_16_out, Reset, Reset);
  nand nand_17 (nand_17_out, SFD, SFD);
  nand nand_18 (nand_18_out, Reset, Reset);
  nand nand_19 (nand_19_out, SFD, SFD);
  nand nand_20 (nand_20_out, Reset, Reset);
  nand nand_21 (nand_21_out, SRD, SRD);
  nand nand_22 (nand_22_out, SW, SW);
  nand nand_23 (nand_23_out, Reset, Reset);
  nand nand_24 (nand_24_out, SRD, SRD);
  nand nand_25 (nand_25_out, Reset, Reset);
  nand nand_26 (nand_26_out, nand_1_out, nand_2_out, nand_3_out, nand_4_out, STL);
  nand nand_27 (nand_27_out, nand_5_out, nand_6_out, nand_7_out, nand_8_out, STG);
  nand nand_28 (nand_28_out, nand_9_out, nand_10_out, nand_11_out, nand_12_out, SW);
  nand nand_29 (nand_29_out, nand_13_out, nand_14_out, nand_15_out, STL);
  nand nand_30 (nand_30_out, nand_16_out, nand_17_out, SFA);
  nand nand_31 (nand_31_out, nand_18_out, nand_19_out, SRD);
  nand nand_32 (nand_32_out, nand_20_out, nand_21_out, nand_22_out, STG);
  nand nand_33 (nand_33_out, nand_23_out, nand_24_out, SFA);
  nand nand_34 (nand_34_out, nand_25_out, SFD);
  nand nand_35 (A2, nand_26_out, nand_27_out, nand_28_out);
  nand nand_36 (A1, nand_29_out, nand_30_out, nand_31_out);
  nand nand_37 (A0, nand_32_out, nand_33_out, nand_34_out);
endmodule
